# Fritzing sketch p5-sorting-machine (saved by Fritzing 0.9.3b)
circuit board: 8.46667cm x 5.64444cm
breadboards: 2

parts:
  Part1 = Arduino Mega 2560 (Rev3)
  M2 = Stepper Motor - Unipolar
  M3 = Stepper Motor - Unipolar
  Q1 = Basic FET P-Channel [package="DPak [SMD]"]
  hc-sr1 = hc-sr04
  U1 = L298 [package=multiwatt15]
  M1 = Stepper Motor - Unipolar
  J4 = Camdenboss CTB0158-6 [part_number=CTB0158-6 package=THT]
  J5 = Camdenboss CTB0158-6 [part_number=CTB0158-6 package=THT]

nets (from the breadboard view):
  N1: Part1.D18/TX1, J4.pin5
  5V: Part1.5V, Q1.drain, hc-sr1.VCC, U1.VS, U1.IN1, U1.VLS, U1.ENB, M1.B, J4.pin2, J4.pin4, J5.pin2, J5.pin4
  GND: Part1.GND, hc-sr1.GND, U1.ENA, U1.IN2, U1.GND, U1.CSB, M1.C, J4.pin1, J4.pin3, J5.pin3
  N2: Part1.D2_PWM, M1.COMMON_2
  N3: Part1.D3_PWM, J5.pin5
  N4: Part1.D23, M1.D
  N5: Part1.D25, U1.IN3
  N6: Part1.D27, U1.IN4
  N7: Part1.D33, hc-sr1.Trig
  N8: Part1.D35, hc-sr1.Echo
  N9: Part1.D52, Q1.Gate
  N10: M2.A, J5.terminal_1
  N11: M2.COMMON_1, J5.terminal_2
  N12: M2.C, J5.terminal_3
  N13: M2.B, J5.terminal_4
  N14: M2.COMMON_2, J5.terminal_5
  N15: M2.D, J5.terminal_6
  N16: M3.A, J4.terminal_1
  N17: M3.COMMON_1, J4.terminal_2
  N18: M3.C, J4.terminal_3
  N19: M3.B, J4.terminal_4
  N20: M3.COMMON_2, J4.terminal_5
  N21: M3.D, J4.terminal_6
  N22: Q1.source, J5.pin1
  N23: U1.OUT3, M1.COMMON_1
  N24: U1.OUT4, M1.A
